// Digital circuit 65816 motherboard decode.dig as structural Verilog
module _65816_motherboard_decode (
  input  A23,
  input  A22,
  input  A21,
  input  A20,
  input  A19,
  input  A18,
  input  A17,
  input  A16,
  input  A15,
  output nRAM_EN_B,
  output nROM_EN_B,
  output nRAMExt_EN_B,
  output nIO_EN_B,
  output nVIDEO_EN_B
);

  wire and_1_out, not_1_out, not_2_out, not_3_out, not_4_out, not_5_out, not_6_out, not_7_out;

  not not_1 (not_1_out, A21);
  not not_2 (not_2_out, A20);
  not not_3 (not_3_out, A19);
  not not_4 (not_4_out, A18);
  not not_5 (not_5_out, A17);
  not not_6 (not_6_out, A16);
  not not_7 (not_7_out, A15);
  or or_1 (nRAM_EN_B, A15, A16, A17, A18, A19, A20, A21, A22, A23);
  and and_1 (and_1_out, not_7_out, not_6_out, not_5_out, not_4_out);
  or or_2 (nRAMExt_EN_B, not_3_out, A20, A21, A22, A23);
  or or_3 (nIO_EN_B, not_2_out, A21, A22, A23);
  or or_4 (nVIDEO_EN_B, not_1_out, A22, A23);
  or or_5 (nROM_EN_B, and_1_out, A19, A20, A21, A22, A23);

  // Notes on the sheet:
  //   nRAM_EN_B: pin 15
  //   nROM_EN_B: pin 16
  //   nRAMExt_EN_B: pin 17
  //   nIO_EN_B: pin 18
  //   nVIDEO_EN_B: pin 19
  //   A23: pin 10
  //   A22: pin 9
  //   A21: pin 8
  //   A20: pin 7
  //   A19: pin 6
  //   A18: pin 5
  //   A17: pin 4
  //   A16: pin 3
  //   A15: pin 2
endmodule
